# Fritzing sketch 328.rf24.sl.th.pcb.v2 (saved by Fritzing 0.9.2b)
circuit board: 5.35cm x 3.55237cm
breadboards: 1

parts:
  ATMEGA_328P = ZIFSOCKET-28-3 [package=dil28-3-zif_socket]
  RADIO = double row female pin header, 8 pins [form="♀ (female)"]
  FTDI = FTDI_BASIC [package=ftdi_basic]
  R2 = Resistor [tolerance=±5% resistance=2.2k package=THT]
  Q1 = PNP-Transistor [package="TO92 [THT]"]
  C2 = Ceramic Capacitor [capacitance=10µF package="100 mil [THT, multilayer]"]
  +_- = male pin header, 2 pins [form="♂ (male)"]
  R1 = Resistor [tolerance=±5% resistance=10k package=THT]
  C1 = Ceramic Capacitor [capacitance=0.1µF voltage=10V package="100 mil [THT, multilayer]"]
  part = Ceramic Capacitor [capacitance=100nF package="100 mil [THT, multilayer]"]  # not connected

nets:
  N1: ATMEGA_328P.P$1, R1.Pin_0, C1.1
  N2: ATMEGA_328P.P$2, FTDI.4
  N3: ATMEGA_328P.P$3, FTDI.5
  N4: ATMEGA_328P.P$7, ATMEGA_328P.P$20, Q1.C, C2.1, +_-.pin2, R1.Pin_1
  N5: ATMEGA_328P.P$14, R2.Pin_0
  N6: ATMEGA_328P.P$16, RADIO.pin7
  N7: ATMEGA_328P.P$17, RADIO.pin6
  N8: ATMEGA_328P.P$18, RADIO.pin4
  N9: ATMEGA_328P.P$19, RADIO.pin3
  N10: ATMEGA_328P.P$22, RADIO.pin1, FTDI.1, C2.0, +_-.pin1
  N11: RADIO.pin8, Q1.E
  N12: FTDI.6, C1.0
  N13: R2.Pin_1, Q1.B

notes:
  www.httech.com.au
  GND
  --JUMPER--
  --REED-SWITCH--
