# Fritzing sketch door_sensor2 (saved by Fritzing 0.8.3b)
circuit board: 6.65669cm x 3.8294cm
breadboards: 1

parts:
  ATMEGA_328P = ZIFSOCKET-28-3 [package=dil28-3-zif_socket]
  RADIO = double row female pin header, 8 pins [form="♀ (female)"]
  FTDI = FTDI_BASIC [package=ftdi_basic]
  C1 = Ceramic Capacitor [capacitance=0.1µF voltage=10V package="100 mil [THT, multilayer]"]
  R1 = Resistor [tolerance=±5% resistance=10k package=THT]
  R2 = Resistor [tolerance=±5% resistance=2.2k package=THT]
  Q1 = PNP-Transistor [package="TO92 [THT]"]

nets:
  N1: ATMEGA_328P.P$1, C1.1, R1.Pin_0
  N2: ATMEGA_328P.P$2, FTDI.4
  N3: ATMEGA_328P.P$3, FTDI.5
  N4: ATMEGA_328P.P$7, ATMEGA_328P.P$20, R1.Pin_1, Q1.C
  N5: ATMEGA_328P.P$11, R2.Pin_0
  N6: ATMEGA_328P.P$15, RADIO.pin2
  N7: ATMEGA_328P.P$16, RADIO.pin7
  N8: ATMEGA_328P.P$17, RADIO.pin6
  N9: ATMEGA_328P.P$18, RADIO.pin4
  N10: ATMEGA_328P.P$19, RADIO.pin3
  N11: ATMEGA_328P.P$22, RADIO.pin1, FTDI.1
  N12: RADIO.pin8, Q1.E
  N13: FTDI.6, C1.0
  N14: R2.Pin_1, Q1.B

notes:
  www.httech.com.au
  Gnd
